// Logisim project RobotPrimitivo.circ as structural Verilog: 29 circuits, main circuit main
module main (
  input  Inicio,
  input  [4:0] in_2
);

  wire clock_1_out, control_de_movimiento_1_a0, control_de_movimiento_1_a1, enable_1_out_2;
  wire [4:0] control_de_movimiento_1_out_2, decodificador_3_5_1_out_4, FlipFlop_out_3, multiplexer_1_out,
       multiplexer_2_out;
  wire [6:0] intodisplay_1_out_3, intodisplay_1_out_4, intodisplay_2_out_3, intodisplay_2_out_4;

  Multiplexer #(.width(5), .enable("false")) multiplexer_1 (
    .in0(in_2), .in1(FlipFlop_out_3), .out(multiplexer_1_out), .sel(Inicio));
  Enable enable_1 (.out_2(enable_1_out_2), .in_1(multiplexer_1_out));
  Control_de_movimiento control_de_movimiento_1 (
    .A1(control_de_movimiento_1_a1), .A0(control_de_movimiento_1_a0), .out_2(control_de_movimiento_1_out_2),
    .in_1(multiplexer_1_out));
  InToDisplay intodisplay_1 (
    .E(1'b1), .in_1(multiplexer_1_out), .out_3(intodisplay_1_out_3), .out_4(intodisplay_1_out_4));
  _7_Segment_Display u_7_segment_display_1 (
    .g(intodisplay_1_out_3[6]), .f(intodisplay_1_out_3[5]), .a(intodisplay_1_out_3[0]),
    .b(intodisplay_1_out_3[1]), .e(intodisplay_1_out_3[4]), .d(intodisplay_1_out_3[3]),
    .c(intodisplay_1_out_3[2]));  // open: dp
  Clock clock_1 (.out(clock_1_out));
  FlipFlop FlipFlop (.in_2(multiplexer_2_out), .in_1(clock_1_out), .out_3(FlipFlop_out_3));
  // Probe on FlipFlop_out_3
  _7_Segment_Display u_7_segment_display_2 (
    .g(intodisplay_1_out_4[6]), .f(intodisplay_1_out_4[5]), .a(intodisplay_1_out_4[0]),
    .b(intodisplay_1_out_4[1]), .e(intodisplay_1_out_4[4]), .d(intodisplay_1_out_4[3]),
    .c(intodisplay_1_out_4[2]));  // open: dp
  Multiplexer #(.width(5), .enable("false")) multiplexer_2 (
    .in0(multiplexer_1_out), .in1(control_de_movimiento_1_out_2), .out(multiplexer_2_out),
    .sel(enable_1_out_2));
  InToDisplay intodisplay_2 (
    .E(enable_1_out_2), .in_1(control_de_movimiento_1_out_2), .out_3(intodisplay_2_out_3),
    .out_4(intodisplay_2_out_4));
  LED Derecha_plus (.in(decodificador_3_5_1_out_4[0]));
  LED Izquierda_plus (.in(decodificador_3_5_1_out_4[1]));
  LED Avanza_plus (.in(decodificador_3_5_1_out_4[2]));
  Decodificador_3_5 decodificador_3_5_1 (
    .A1(control_de_movimiento_1_a1), .A0(control_de_movimiento_1_a0), .Enable(enable_1_out_2),
    .out_4(decodificador_3_5_1_out_4));
  LED STOP_minus (.in(decodificador_3_5_1_out_4[3]));
  LED Invalido (.in(decodificador_3_5_1_out_4[4]));
  _7_Segment_Display u_7_segment_display_3 (
    .g(intodisplay_2_out_4[6]), .f(intodisplay_2_out_4[5]), .a(intodisplay_2_out_4[0]),
    .b(intodisplay_2_out_4[1]), .e(intodisplay_2_out_4[4]), .d(intodisplay_2_out_4[3]),
    .c(intodisplay_2_out_4[2]));  // open: dp
  _7_Segment_Display u_7_segment_display_4 (
    .g(intodisplay_2_out_3[6]), .f(intodisplay_2_out_3[5]), .a(intodisplay_2_out_3[0]),
    .b(intodisplay_2_out_3[1]), .e(intodisplay_2_out_3[4]), .d(intodisplay_2_out_3[3]),
    .c(intodisplay_2_out_3[2]));  // open: dp
endmodule

// Movimiento
module Control_de_movimiento (
  input  [4:0] in_1,
  output [4:0] out_2,
  output A1,
  output A0
);

  SALIDA4 salida4_1 (.V(in_1[4]), .W(in_1[3]), .X(in_1[2]), .Y(in_1[1]), .Z(in_1[0]), .out_6(out_2[4]));
  SALIDA3 salida3_1 (.out_6(out_2[3]), .V(in_1[4]), .W(in_1[3]), .X(in_1[2]), .Y(in_1[1]), .Z(in_1[0]));
  SALIDA2 salida2_1 (.out_6(out_2[2]), .V(in_1[4]), .W(in_1[3]), .X(in_1[2]), .Y(in_1[1]), .Z(in_1[0]));
  SALIDA1 salida1_1 (.out_6(out_2[1]), .V(in_1[4]), .W(in_1[3]), .X(in_1[2]), .Y(in_1[1]), .Z(in_1[0]));
  SALIDA0 salida0_1 (.out_6(out_2[0]), .V(in_1[4]), .W(in_1[3]), .X(in_1[2]), .Y(in_1[1]), .Z(in_1[0]));
  Accion1 accion1_1 (.out_6(A1), .V(in_1[4]), .W(in_1[3]), .X(in_1[2]), .Y(in_1[1]), .Z(in_1[0]));
  Accion0 accion0_1 (.out_6(A0), .V(in_1[4]), .W(in_1[3]), .X(in_1[2]), .Y(in_1[1]), .Z(in_1[0]));
endmodule

module SALIDA4 (
  input  V,
  input  W,
  input  X,
  input  Y,
  input  Z,
  output out_6
);

  wire and_1_out, and_2_out, and_3_out, and_4_out, and_5_out, and_6_out, and_7_out, and_8_out;

  and and_1 (and_1_out, V, ~X, ~Y);  // AND_Gate
  and and_2 (and_2_out, V, W, ~Z);  // AND_Gate
  and and_3 (and_3_out, ~V, ~W, ~X, Y);  // AND_Gate
  and and_4 (and_4_out, ~V, ~W, Y, Z);  // AND_Gate
  and and_5 (and_5_out, ~W, ~X, Y, Z);  // AND_Gate
  and and_6 (and_6_out, ~V, ~W, X, ~Y);  // AND_Gate
  and and_7 (and_7_out, ~W, X, ~Y, Z);  // AND_Gate
  and and_8 (and_8_out, ~V, W, ~Y, Z);  // AND_Gate
  or or_1 (out_6, and_1_out, and_3_out, and_2_out, and_4_out, and_5_out, and_6_out, and_7_out, and_8_out);
endmodule

module SALIDA3 (
  input  V,
  input  W,
  input  X,
  input  Y,
  input  Z,
  output out_6
);

  wire and_1_out, and_2_out, and_3_out, and_4_out, and_5_out;

  and and_1 (and_1_out, V, ~X);  // AND_Gate
  and and_2 (and_2_out, V, Z);
  and and_3 (and_3_out, ~X, ~Y, ~Z);  // AND_Gate
  and and_4 (and_4_out, W, Y, Z);
  and and_5 (and_5_out, ~W, X, ~Y, Z);  // AND_Gate
  or or_1 (out_6, and_1_out, and_2_out, and_3_out, and_4_out, and_5_out);
endmodule

module SALIDA2 (
  input  V,
  input  W,
  input  X,
  input  Y,
  input  Z,
  output out_6
);

  wire and_1_out, and_2_out, and_3_out, and_4_out, and_5_out, and_6_out, and_7_out;

  and and_1 (and_1_out, ~V, ~Y, Z);  // AND_Gate
  and and_2 (and_2_out, ~V, ~W, ~X);  // AND_Gate
  and and_3 (and_3_out, ~V, ~X, ~Y);  // AND_Gate
  and and_4 (and_4_out, ~W, ~X, ~Z);  // AND_Gate
  and and_5 (and_5_out, ~V, ~W, Y, ~Z);  // AND_Gate
  and and_6 (and_6_out, V, ~W, ~Y, ~Z);  // AND_Gate
  and and_7 (and_7_out, V, X, Z, Y);
  or or_1 (out_6, and_1_out, and_2_out, and_3_out, and_4_out, and_5_out, and_6_out, and_7_out);
endmodule

module SALIDA1 (
  input  V,
  input  W,
  input  X,
  input  Y,
  input  Z,
  output out_6
);

  wire and_1_out, and_2_out, and_3_out, and_4_out, and_5_out, and_6_out, and_7_out;

  and and_1 (and_1_out, X, ~Y, ~Z);  // AND_Gate
  and and_2 (and_2_out, X, Y, Z);
  and and_3 (and_3_out, V, ~Y, ~Z);  // AND_Gate
  and and_4 (and_4_out, V, W, X);
  and and_5 (and_5_out, ~V, ~X, ~Y, Z);  // AND_Gate
  and and_6 (and_6_out, ~V, ~X, Y, ~Z);  // AND_Gate
  and and_7 (and_7_out, V, ~W, Y, Z);  // AND_Gate
  or or_1 (out_6, and_1_out, and_2_out, and_3_out, and_4_out, and_5_out, and_6_out, and_7_out);
endmodule

module SALIDA0 (
  input  V,
  input  W,
  input  X,
  input  Y,
  input  Z,
  output out_6
);

  wire and_1_out, and_2_out, and_3_out, and_4_out, and_5_out;

  and and_1 (and_1_out, W, ~Y, Z);  // AND_Gate
  and and_2 (and_2_out, V, ~W, Y);  // AND_Gate
  and and_3 (and_3_out, ~V, ~W, ~Y);  // AND_Gate
  and and_4 (and_4_out, W, Y, ~Z);  // AND_Gate
  and and_5 (and_5_out, ~V, W, ~X, Z);  // AND_Gate
  or or_1 (out_6, and_1_out, and_2_out, and_3_out, and_4_out, and_5_out);
endmodule

module Accion1 (
  input  V,
  input  W,
  input  X,
  input  Y,
  input  Z,
  output out_6
);

  wire and_1_out, and_2_out, and_3_out, and_4_out, and_5_out, and_6_out;

  and and_1 (and_1_out, V, W);
  and and_2 (and_2_out, W, Z);
  and and_3 (and_3_out, ~V, X, Z);  // AND_Gate
  and and_4 (and_4_out, ~X, Y, Z);  // AND_Gate
  and and_5 (and_5_out, ~V, ~X, Y);  // AND_Gate
  and and_6 (and_6_out, X, ~Y, ~Z);  // AND_Gate
  or or_1 (out_6, and_1_out, and_2_out, and_3_out, and_4_out, and_5_out, and_6_out);
endmodule

module InToDisplay (
  input  [4:0] in_1,
  input  E,
  output [6:0] out_3,
  output [6:0] out_4
);

  Decimal decimal_1 (
    .A1(out_3[0]), .B1(out_3[1]), .C1(out_3[2]), .D1(out_3[3]), .E1(out_3[4]), .G1(out_3[6]), .v(in_1[4]),
    .w(in_1[3]), .x(in_1[2]), .y(in_1[1]), .z(in_1[0]), .Enable(E), .F1(out_3[5]));
  Unidad unidad_1 (
    .A(out_4[0]), .B(out_4[1]), .C(out_4[2]), .D(out_4[3]), .E(out_4[4]), .F(out_4[5]), .G(out_4[6]),
    .v(in_1[4]), .w(in_1[3]), .x(in_1[2]), .y(in_1[1]), .z(in_1[0]), .Enable(E));
endmodule

module Accion0 (
  input  V,
  input  W,
  input  X,
  input  Y,
  input  Z,
  output out_6
);

  wire and_1_out, and_2_out, and_3_out, and_4_out, and_5_out;

  and and_1 (and_1_out, ~W, ~X, ~Y);  // AND_Gate
  and and_2 (and_2_out, X, Y, ~Z);  // AND_Gate
  and and_3 (and_3_out, V, X, Y);
  and and_4 (and_4_out, ~V, ~X, ~Y, ~Z);  // AND_Gate
  and and_5 (and_5_out, V, ~X, ~Y, Z);  // AND_Gate
  or or_1 (out_6, and_1_out, and_2_out, and_3_out, and_4_out, and_5_out);
endmodule

module Decimal (
  input  v,
  input  w,
  input  x,
  input  y,
  input  z,
  input  Enable,
  output A1,
  output B1,
  output C1,
  output D1,
  output E1,
  output F1,
  output G1
);

  wire A1_out_6, C1_out_6, D1_out_6, E1_out_6, F1_out_6, G1_out_6;

  A1 u_A1 (.out_6(A1_out_6), .v(v), .w(w), .x(x), .y(y), .z(z));
  C1 u_C1 (.out_6(C1_out_6), .v(v), .w(w), .x(x), .y(y), .z(z));
  D1 u_D1 (.out_6(D1_out_6), .v(v), .w(w), .x(x), .y(y), .z(z));
  E1 u_E1 (.out_6(E1_out_6), .v(v), .w(w), .x(x), .y(y), .z(z));
  F1 u_F1 (.out_6(F1_out_6), .v(v), .w(w), .x(x), .y(y), .z(z));
  G1 u_G1 (.out_6(G1_out_6), .v(v), .w(w), .x(x), .y(y), .z(z));
  and and_1 (A1, Enable, A1_out_6);
  and and_2 (B1, Enable, 1'b1);
  and and_3 (C1, Enable, C1_out_6);
  and and_4 (D1, Enable, D1_out_6);
  and and_5 (E1, Enable, E1_out_6);
  and and_6 (F1, Enable, F1_out_6);
  and and_7 (G1, Enable, G1_out_6);
endmodule

module A1 (
  input  v,
  input  w,
  input  x,
  input  y,
  input  z,
  output out_6
);

  wire and_1_out, and_2_out, and_3_out, and_4_out, not_1_out, not_2_out, not_3_out, not_4_out, not_5_out,
       not_6_out;

  not not_1 (not_1_out, v);
  not not_2 (not_2_out, w);
  not not_3 (not_3_out, w);
  not not_4 (not_4_out, v);
  not not_5 (not_5_out, x);
  not not_6 (not_6_out, y);
  and and_1 (and_1_out, not_1_out, not_2_out);
  and and_2 (and_2_out, not_3_out, x);
  and and_3 (and_3_out, v, w);
  and and_4 (and_4_out, not_4_out, not_5_out, not_6_out);
  or or_1 (out_6, and_1_out, and_2_out, and_3_out, and_4_out);
endmodule

module C1 (
  input  v,
  input  w,
  input  x,
  input  y,
  input  z,
  output out_6
);

  wire and_1_out, and_2_out, not_1_out, not_2_out, not_3_out;

  not not_1 (not_1_out, w);
  not not_2 (not_2_out, x);
  and and_1 (and_1_out, not_1_out, not_2_out);
  and and_2 (and_2_out, w, x, y);
  not not_3 (not_3_out, v);
  or or_1 (out_6, and_1_out, and_2_out, not_3_out);
endmodule

module D1 (
  input  v,
  input  w,
  input  x,
  input  y,
  input  z,
  output out_6
);

  wire and_1_out, and_2_out, and_3_out, and_4_out, not_1_out, not_2_out, not_3_out, not_4_out, not_5_out,
       not_6_out;

  not not_1 (not_1_out, v);
  and and_1 (and_1_out, not_1_out, not_2_out);
  not not_2 (not_2_out, w);
  not not_3 (not_3_out, w);
  and and_2 (and_2_out, not_3_out, x);
  and and_3 (and_3_out, v, w);
  not not_4 (not_4_out, v);
  and and_4 (and_4_out, not_4_out, not_5_out, not_6_out);
  not not_5 (not_5_out, x);
  not not_6 (not_6_out, y);
  or or_1 (out_6, and_1_out, and_2_out, and_3_out, and_4_out);
endmodule

module E1 (
  input  v,
  input  w,
  input  x,
  input  y,
  input  z,
  output out_6
);

  wire and_1_out, and_2_out, and_3_out, and_4_out, and_5_out, not_1_out, not_2_out, not_3_out, not_4_out,
       not_5_out, not_6_out, not_7_out, not_8_out;

  not not_1 (not_1_out, v);
  and and_1 (and_1_out, not_1_out, not_2_out);
  not not_2 (not_2_out, w);
  not not_3 (not_3_out, w);
  and and_2 (and_2_out, not_3_out, x);
  not not_4 (not_4_out, v);
  and and_3 (and_3_out, not_4_out, not_5_out, not_6_out);
  not not_5 (not_5_out, x);
  not not_6 (not_6_out, y);
  and and_4 (and_4_out, v, w, not_7_out);
  not not_7 (not_7_out, x);
  and and_5 (and_5_out, v, x, not_8_out);
  not not_8 (not_8_out, y);
  or or_1 (out_6, and_1_out, and_2_out, and_3_out, and_4_out, and_5_out);
endmodule

module F1 (
  input  v,
  input  w,
  input  x,
  input  y,
  input  z,
  output out_6
);

  wire and_1_out, and_2_out, not_1_out, not_2_out, not_3_out, not_4_out, not_5_out;

  not not_1 (not_1_out, v);
  not not_2 (not_2_out, w);
  not not_3 (not_3_out, v);
  not not_4 (not_4_out, x);
  not not_5 (not_5_out, y);
  and and_1 (and_1_out, not_1_out, not_2_out);
  and and_2 (and_2_out, not_3_out, not_4_out, not_5_out);
  or or_1 (out_6, and_1_out, and_2_out);
endmodule

module G1 (
  input  v,
  input  w,
  input  x,
  input  y,
  input  z,
  output out_6
);

  wire and_1_out, and_2_out;

  and and_1 (and_1_out, v, x);
  or or_1 (out_6, and_1_out, and_2_out);
  and and_2 (and_2_out, v, w);
endmodule

module Unidad (
  input  Enable,
  input  v,
  input  w,
  input  x,
  input  y,
  input  z,
  output A,
  output B,
  output C,
  output D,
  output E,
  output F,
  output G
);

  wire a_out_6, b_out_6, c_out_6, d_out_6, e_out_6, f_out_6, g_out_6;

  a u_a (.out_6(a_out_6), .v(v), .w(w), .x(x), .y(y), .z(z));
  b u_b (.out_6(b_out_6), .v(v), .w(w), .x(x), .y(y), .z(z));
  c u_c (.out_6(c_out_6), .v(v), .w(w), .x(x), .y(y), .z(z));
  d u_d (.out_6(d_out_6), .v(v), .w(w), .x(x), .y(y), .z(z));
  e u_e (.out_6(e_out_6), .v(v), .w(w), .x(x), .y(y), .z(z));
  f u_f (.out_6(f_out_6), .v(v), .w(w), .x(x), .y(y), .z(z));
  g u_g (.out_6(g_out_6), .v(v), .w(w), .x(x), .y(y), .z(z));
  and and_1 (A, Enable, a_out_6);
  and and_2 (B, Enable, b_out_6);
  and and_3 (C, Enable, c_out_6);
  and and_4 (D, Enable, d_out_6);
  and and_5 (E, Enable, e_out_6);
  and and_6 (F, Enable, f_out_6);
  and and_7 (G, Enable, g_out_6);
endmodule

module a (
  input  v,
  input  w,
  input  x,
  input  y,
  input  z,
  output out_6
);

  wire and_1_out, and_2_out, and_3_out, and_4_out, and_5_out, and_6_out, and_7_out, and_8_out, not_1_out,
       not_2_out, not_3_out, not_4_out, not_5_out, not_6_out, not_7_out, not_8_out, not_9_out, not_10_out,
       not_11_out, not_12_out;

  not not_1 (not_1_out, w);
  not not_2 (not_2_out, v);
  not not_3 (not_3_out, x);
  not not_4 (not_4_out, z);
  not not_5 (not_5_out, v);
  not not_6 (not_6_out, v);
  not not_7 (not_7_out, y);
  not not_8 (not_8_out, y);
  not not_9 (not_9_out, w);
  not not_10 (not_10_out, z);
  not not_11 (not_11_out, x);
  not not_12 (not_12_out, z);
  and and_1 (and_1_out, not_1_out, y);
  and and_2 (and_2_out, not_2_out, not_3_out, not_4_out);
  and and_3 (and_3_out, not_5_out, x, z);
  and and_4 (and_4_out, not_6_out, w, not_7_out);
  and and_5 (and_5_out, w, x, not_8_out);
  and and_6 (and_6_out, v, not_9_out, not_10_out);
  and and_7 (and_7_out, v, not_11_out, z);
  and and_8 (and_8_out, v, y, not_12_out);
  or or_1 (out_6, and_1_out, and_2_out, and_3_out, and_4_out, and_5_out, and_6_out, and_7_out, and_8_out);
endmodule

module b (
  input  v,
  input  w,
  input  x,
  input  y,
  input  z,
  output out_6
);

  wire and_1_out, and_2_out, and_3_out, and_4_out, and_5_out, and_6_out, and_7_out, and_8_out, and_9_out,
       not_1_out, not_2_out, not_3_out, not_4_out, not_5_out, not_6_out, not_7_out, not_8_out, not_9_out,
       not_10_out, not_11_out, not_12_out, not_13_out, not_14_out, not_15_out;

  not not_1 (not_1_out, v);
  not not_2 (not_2_out, y);
  not not_3 (not_3_out, z);
  not not_4 (not_4_out, w);
  not not_5 (not_5_out, x);
  not not_6 (not_6_out, w);
  not not_7 (not_7_out, x);
  not not_8 (not_8_out, w);
  not not_9 (not_9_out, x);
  not not_10 (not_10_out, v);
  not not_11 (not_11_out, y);
  not not_12 (not_12_out, v);
  not not_13 (not_13_out, z);
  not not_14 (not_14_out, y);
  not not_15 (not_15_out, z);
  and and_1 (and_1_out, v, x);
  and and_2 (and_2_out, not_1_out, not_2_out, not_3_out);
  and and_3 (and_3_out, not_4_out, not_5_out, z);
  and and_4 (and_4_out, not_6_out, not_7_out, y);
  and and_5 (and_5_out, not_8_out, y, z);
  and and_6 (and_6_out, not_9_out, y, z);
  and and_7 (and_7_out, not_10_out, w, not_11_out);
  and and_8 (and_8_out, not_12_out, w, not_13_out);
  and and_9 (and_9_out, w, not_14_out, not_15_out);
  or or_1 (out_6, and_1_out, and_2_out, and_3_out, and_4_out, and_5_out, and_6_out, and_7_out, and_8_out, and_9_out);
endmodule

module c (
  input  v,
  input  w,
  input  x,
  input  y,
  input  z,
  output out_6
);

  wire and_1_out, and_2_out, and_3_out, and_4_out, and_5_out, not_1_out, not_2_out, not_3_out, not_4_out,
       not_5_out, not_6_out;

  not not_1 (not_1_out, x);
  not not_2 (not_2_out, y);
  not not_3 (not_3_out, x);
  not not_4 (not_4_out, y);
  not not_5 (not_5_out, v);
  not not_6 (not_6_out, w);
  and and_1 (and_1_out, not_1_out, not_2_out);
  and and_2 (and_2_out, w, y);
  and and_3 (and_3_out, v, not_3_out);
  and and_4 (and_4_out, v, not_4_out);
  and and_5 (and_5_out, not_5_out, not_6_out, x);
  or or_1 (out_6, z, and_1_out, and_2_out, and_3_out, and_4_out, and_5_out);
endmodule

module d (
  input  v,
  input  w,
  input  x,
  input  y,
  input  z,
  output out_6
);

  wire and_1_out, and_2_out, and_3_out, and_4_out, and_5_out, and_6_out, and_7_out, and_8_out, and_9_out,
       and_10_out, not_1_out, not_2_out, not_3_out, not_4_out, not_5_out, not_6_out, not_7_out, not_8_out,
       not_9_out, not_10_out, not_11_out, not_12_out, not_13_out, not_14_out, not_15_out, not_16_out;

  not not_1 (not_1_out, v);
  not not_2 (not_2_out, x);
  not not_3 (not_3_out, z);
  not not_4 (not_4_out, w);
  not not_5 (not_5_out, x);
  not not_6 (not_6_out, w);
  not not_7 (not_7_out, z);
  not not_8 (not_8_out, y);
  not not_9 (not_9_out, y);
  not not_10 (not_10_out, w);
  not not_11 (not_11_out, z);
  not not_12 (not_12_out, w);
  not not_13 (not_13_out, z);
  not not_14 (not_14_out, v);
  not not_15 (not_15_out, y);
  not not_16 (not_16_out, v);
  and and_1 (and_1_out, not_1_out, not_2_out, not_3_out);
  and and_2 (and_2_out, not_4_out, not_5_out, y);
  and and_3 (and_3_out, not_6_out, y, not_7_out);
  and and_4 (and_4_out, w, not_8_out, z);
  and and_5 (and_5_out, w, x, not_9_out);
  and and_6 (and_6_out, v, not_10_out, not_11_out);
  and and_7 (and_7_out, v, not_12_out, y);
  and and_8 (and_8_out, v, y, not_13_out);
  and and_9 (and_9_out, not_14_out, x, not_15_out, z);
  and and_10 (and_10_out, not_16_out, w, x, z);
  or or_1 (out_6, and_1_out, and_2_out, and_3_out, and_4_out, and_5_out, and_6_out, and_7_out, and_8_out, and_9_out, and_10_out);
endmodule

module e (
  input  v,
  input  w,
  input  x,
  input  y,
  input  z,
  output out_6
);

  wire and_1_out, and_2_out, and_3_out, and_4_out, and_5_out, not_1_out, not_2_out, not_3_out, not_4_out,
       not_5_out, not_6_out, not_7_out, not_8_out, not_9_out, not_10_out, not_11_out;

  not not_1 (not_1_out, w);
  not not_2 (not_2_out, x);
  not not_3 (not_3_out, z);
  not not_4 (not_4_out, w);
  not not_5 (not_5_out, z);
  not not_6 (not_6_out, x);
  not not_7 (not_7_out, z);
  not not_8 (not_8_out, z);
  not not_9 (not_9_out, v);
  not not_10 (not_10_out, y);
  not not_11 (not_11_out, z);
  and and_1 (and_1_out, not_1_out, not_2_out, not_3_out);
  and and_2 (and_2_out, not_4_out, y, not_5_out);
  and and_3 (and_3_out, not_6_out, y, not_7_out);
  and and_4 (and_4_out, v, x, not_8_out);
  and and_5 (and_5_out, not_9_out, w, not_10_out, not_11_out);
  or or_1 (out_6, and_1_out, and_2_out, and_3_out, and_4_out, and_5_out);
endmodule

module f (
  input  v,
  input  w,
  input  x,
  input  y,
  input  z,
  output out_6
);

  wire and_1_out, and_2_out, and_3_out, and_4_out, and_5_out, and_6_out, and_7_out, and_8_out, not_1_out,
       not_2_out, not_3_out, not_4_out, not_5_out, not_6_out, not_7_out, not_8_out, not_9_out, not_10_out,
       not_11_out, not_12_out, not_13_out, not_14_out, not_15_out, not_16_out;

  not not_1 (not_1_out, w);
  not not_2 (not_2_out, y);
  not not_3 (not_3_out, z);
  not not_4 (not_4_out, x);
  not not_5 (not_5_out, y);
  not not_6 (not_6_out, z);
  not not_7 (not_7_out, y);
  not not_8 (not_8_out, v);
  not not_9 (not_9_out, w);
  not not_10 (not_10_out, y);
  not not_11 (not_11_out, v);
  not not_12 (not_12_out, w);
  not not_13 (not_13_out, z);
  not not_14 (not_14_out, v);
  not not_15 (not_15_out, w);
  not not_16 (not_16_out, x);
  and and_1 (and_1_out, not_1_out, not_2_out, not_3_out);
  and and_2 (and_2_out, w, not_4_out, not_5_out);
  and and_3 (and_3_out, w, y, not_6_out);
  and and_4 (and_4_out, v, w, not_7_out);
  and and_5 (and_5_out, not_8_out, not_9_out, x, not_10_out);
  and and_6 (and_6_out, not_11_out, not_12_out, x, not_13_out);
  and and_7 (and_7_out, not_14_out, w, x, y);
  and and_8 (and_8_out, v, not_15_out, not_16_out, y);
  or or_1 (out_6, and_1_out, and_2_out, and_3_out, and_4_out, and_5_out, and_6_out, and_7_out, and_8_out);
endmodule

module g (
  input  v,
  input  w,
  input  x,
  input  y,
  input  z,
  output out_6
);

  wire and_1_out, and_2_out, and_3_out, and_4_out, and_5_out, and_6_out, and_7_out, not_1_out, not_2_out,
       not_3_out, not_4_out, not_5_out, not_6_out, not_7_out, not_8_out, not_9_out, not_10_out, not_11_out;

  not not_1 (not_1_out, y);
  not not_2 (not_2_out, w);
  not not_3 (not_3_out, x);
  not not_4 (not_4_out, w);
  not not_5 (not_5_out, z);
  not not_6 (not_6_out, v);
  not not_7 (not_7_out, y);
  not not_8 (not_8_out, v);
  not not_9 (not_9_out, x);
  not not_10 (not_10_out, z);
  not not_11 (not_11_out, w);
  and and_1 (and_1_out, w, not_1_out);
  and and_2 (and_2_out, not_2_out, not_3_out, y);
  and and_3 (and_3_out, not_4_out, y, not_5_out);
  and and_4 (and_4_out, not_6_out, x, not_7_out);
  and and_5 (and_5_out, not_8_out, w, x);
  and and_6 (and_6_out, v, not_9_out, not_10_out);
  and and_7 (and_7_out, v, not_11_out, y);
  or or_1 (out_6, and_1_out, and_2_out, and_3_out, and_4_out, and_5_out, and_6_out, and_7_out);
endmodule

module Decodificador_3_5 (
  input  Enable,
  input  A1,
  input  A0,
  output [4:0] out_4
);

  wire not_1_out, not_2_out, not_3_out, not_4_out;

  not not_1 (not_1_out, A0);
  not not_2 (not_2_out, A1);
  not not_3 (not_3_out, A1);
  not not_4 (not_4_out, A0);
  and and_1 (out_4[0], not_1_out, Enable, not_2_out);
  and and_2 (out_4[1], A0, Enable, not_3_out);
  and and_3 (out_4[2], not_4_out, Enable, A1);
  and and_4 (out_4[3], A0, Enable, A1);
  not not_5 (out_4[4], Enable);
endmodule

module Enable (
  input  [4:0] in_1,
  output out_2
);

  wire and_1_out, and_2_out, and_3_out, and_4_out, and_5_out, and_6_out;

  and and_1 (and_1_out, ~in_1[4], in_1[0]);  // AND_Gate
  and and_2 (and_2_out, ~in_1[3], in_1[1]);  // AND_Gate
  and and_3 (and_3_out, ~in_1[3], in_1[2]);  // AND_Gate
  and and_4 (and_4_out, in_1[3], ~in_1[2]);  // AND_Gate
  and and_5 (and_5_out, ~in_1[4], in_1[2], ~in_1[1]);  // AND_Gate
  and and_6 (and_6_out, in_1[2], ~in_1[1], in_1[0]);  // AND_Gate
  or or_1 (out_2, and_1_out, and_2_out, and_3_out, and_4_out, and_5_out, and_6_out);
endmodule

module Pruebita (
  input  V,
  input  W,
  input  X,
  input  Y,
  input  Z,
  input  Boton,
  output out_7,
  output out_8,
  output out_9,
  output out_10,
  output out_11
);

  wire not_1_out;

  not not_1 (not_1_out, Boton);
  and and_1 (out_7, not_1_out, V);
  and and_2 (out_9, not_1_out, X);
  and and_3 (out_8, not_1_out, W);
  and and_4 (out_10, not_1_out, Y);
  and and_5 (out_11, not_1_out, Z);
endmodule

module FlipFlop (
  input  in_1,
  input  [4:0] in_2,
  output [4:0] out_3
);

  D_Flip_Flop d_ff_1 (.clk(in_1), .D(in_2[0]), .Q(out_3[0]));  // open: Qn, preset, en, reset
  D_Flip_Flop d_ff_2 (.clk(in_1), .D(in_2[1]), .Q(out_3[1]));  // open: Qn, preset, en, reset
  D_Flip_Flop d_ff_3 (.clk(in_1), .D(in_2[2]), .Q(out_3[2]));  // open: Qn, preset, en, reset
  D_Flip_Flop d_ff_4 (.clk(in_1), .D(in_2[3]), .Q(out_3[3]));  // open: Qn, preset, en, reset
  D_Flip_Flop d_ff_5 (.clk(in_1), .D(in_2[4]), .Q(out_3[4]));  // open: Qn, preset, en, reset
endmodule
